# Fritzing sketch Circuit (saved by Fritzing 0.8.7b)
perfboards: 1

parts:
  U1 = lolin
  SN75176BP = IC, DIP package, 8 pins [chip_label=IC]
  J1 = male pin header, 4 pins [form="♂ (male)"]
  LM2940CT5 = Voltage Regulator [package=to-220-alt]
  C2 = Electrolytic Capacitor [capacitance=1µF voltage=16V package="100 mil [THT, electrolytic]"]
  R1 = Resistor [tolerance=±1% resistance=150 package=THT]
  LED1 = LED - 3mm [color="Green (570nm)" package="3 mm [THT]"]
  C1 = Electrolytic Capacitor [capacitance=10µF voltage=16V package="100 mil [THT, electrolytic]"]
  D1_(3x_in_series) = Rectifier Diode [part_number=1N4001 package="300 mil [THT]"]

nets:
  N1: U1.connector14, SN75176BP.pin8, LM2940CT5.OUT, C2.+, R1.Pin_1
  N2: U1.connector23, SN75176BP.pin1
  N3: U1.connector24, SN75176BP.pin4
  N4: SN75176BP.pin2, SN75176BP.pin3
  N5: SN75176BP.pin5, J1.pin2, LM2940CT5.GND, C2.-, LED1.cathode, C1.-
  N6: SN75176BP.pin6, J1.pin4
  N7: SN75176BP.pin7, J1.pin3
  N8: J1.pin1, D1_(3x_in_series).anode
  N9: LM2940CT5.IN, C1.+, D1_(3x_in_series).cathode
  N10: R1.Pin_0, LED1.anode

notes:
  Perfboard 7x5
  PORT A
  PORT B
  GND
  +12VDC
  WALL REMOTE CABLE
